# Fritzing sketch breadboard (saved by Fritzing 1.0.4)

parts:
  Part1 = Arduino Uno (Rev3) - ICSP
  Grove1 = Grove Buzz

nets:
  GND: Part1.GND, Grove1.GND
  N1: Part1.D3_PWM, Grove1.SIG
  5V: Part1.5V, Grove1.VCC

notes:
  SIG
  NC
  VCC
  GND
